# Fritzing sketch 01-LED-blinky-01 (saved by Fritzing 0.9.3b)
breadboards: 1

parts:
  Raspberry_Pi = Raspberry Pi 3 [part_number=RPI-3-V1.2]
  R1 = Resistor [tolerance=±5% resistance=330 package=THT]
  LED1 = LED - 3mm [color="White (6500K)" package="3 mm [THT]"]

nets:
  N1: Raspberry_Pi.GND, R1.Pin_1
  N2: Raspberry_Pi.GIPO23, LED1.anode
  N3: R1.Pin_0, LED1.cathode

notes:
  GPIO23 ----- LED ----+
  |
  330Ω
  |
  GND ------------------- +
  LED
  anode (positive, +) : longer pin
  cathode (negative, -) : shorter pin
