# Fritzing sketch 02-hello-button-01 (saved by Fritzing 0.9.3b)
breadboards: 1

parts:
  Raspberry_Pi = Raspberry Pi 3 [part_number=RPI-3-V1.2]
  R1 = Resistor [tolerance=±5% resistance=10k package=THT]
  SW1 = Momentary Switch [package=ksa_sealed_tac_switch]

nets:
  3V3: Raspberry_Pi.3v3, Raspberry_Pi.3V3, SW1.4
  N1: Raspberry_Pi.GIPO24, R1.Pin_1
  N2: R1.Pin_0, SW1.2

notes:
  3.3V ------- Button - Button -------+
  |
  GPIO24 -- R1 (103 = 10Kohm) ---+
  |
  Internal pull-down resistor (50Kohm)
  |
  GND
  Resistor R1 is to protect GPIO when you carelessly set the GPIO to output mode.
  button on: high = 1= True
  button off: low = 0 = False
  Internal pull-down resistor
  (50K ohm) used.
