# Fritzing sketch 06-light-sensor-01 (saved by Fritzing 0.9.3b)
breadboards: 1

parts:
  Raspberry_Pi = Raspberry Pi 3 [part_number=RPI-3-V1.2]
  R1 = PHOTOCELL [part_number="1M Ohm" package=photocell]
  C1 = Ceramic Capacitor [capacitance="100 nF" package="0805 [SMD, multilayer]"]

nets:
  N1: Raspberry_Pi.3v3, R1.P$1
  N2: Raspberry_Pi.GND, C1.1
  N3: Raspberry_Pi.GIPO18, R1.P$2, C1.0

notes:
  3.3V --------------------+
  |
  |
  |
  GPIO18 <---- CdS Photo Cell (1M Ohm)
  input |
  pulldown |
  |
  |
  GND ---------- Ceramic Capacitor (100nF)
