# Fritzing sketch 4-button (saved by Fritzing 0.9.3b)
breadboards: 1

parts:
  Raspberry_Pi_1 = Raspberry Pi 3 [part_number=RPI-3-V1.2]
  R1 = Resistor [tolerance=±5% resistance=10k package="0603 [SMD]"]
  S1 = Momentary Switch [package=ksa_sealed_tac_switch]
  S2 = Momentary Switch [package=ksa_sealed_tac_switch]
  S3 = Momentary Switch [package=ksa_sealed_tac_switch]
  S4 = Momentary Switch [package=ksa_sealed_tac_switch]
  R3 = Resistor [tolerance=±5% resistance=10k package="0603 [SMD]"]
  R4 = Resistor [tolerance=±5% resistance=10k package="0603 [SMD]"]
  R5 = Resistor [tolerance=±5% resistance=10k package="0603 [SMD]"]

nets:
  N1: Raspberry_Pi_1.GIPO10, S1.2, S2.2, S3.2, S4.2
  N2: Raspberry_Pi_1.GIPO8, R1.Pin_0
  N3: Raspberry_Pi_1.GIPO25, R5.Pin_0
  N4: Raspberry_Pi_1.GIPO24, R4.Pin_0
  N5: Raspberry_Pi_1.GIPO23, R3.Pin_0
  N6: R1.Pin_1, S1.3
  N7: S2.3, R5.Pin_1
  N8: S3.3, R3.Pin_1
  N9: S4.3, R4.Pin_1
