# Fritzing sketch pot (saved by Fritzing 0.9.3b)
breadboards: 1

parts:
  R1 = Resistor [tolerance=±5% resistance=100 package=THT]
  LED1 = smd LED [color="Red (633nm)" package="0603 [SMD]"]
  R3 = TRIMPOT [package=3386u]
  Raspberry_Pi_1 = Raspberry Pi 3 [part_number=RPI-3-V1.2]

nets:
  N1: R1.Pin_0, LED1.cathode
  N2: R1.Pin_1, R3.CCW
  N3: LED1.anode, Raspberry_Pi_1.3v3
  N4: R3.WIPER, Raspberry_Pi_1.GND
