# Fritzing sketch supersonic-distance (saved by Fritzing 0.9.3b)
breadboards: 1

parts:
  Raspberry_Pi = Raspberry Pi 3 [part_number=RPI-3-V1.2]
  Supersonic_Distance_Sensor = hc-sr04
  R1 = Resistor [tolerance=±5% resistance=1k package=THT]
  R2 = Resistor [tolerance=±5% resistance=1.5k package=THT]
  LED1 = smd LED [color="Red (633nm)" package="0603 [SMD]"]
  R3 = Resistor [tolerance=±5% resistance=220 package=THT]

nets:
  GND: Raspberry_Pi.GND, Supersonic_Distance_Sensor.GND, R2.Pin_1, R3.Pin_0
  N1: Raspberry_Pi.GIPO21, R1.Pin_0, R2.Pin_0
  N2: Raspberry_Pi.GIPO20, Supersonic_Distance_Sensor.Trig
  N3: Raspberry_Pi.GIPO16, LED1.anode
  5V: Raspberry_Pi.5V, Supersonic_Distance_Sensor.VCC
  N4: Supersonic_Distance_Sensor.Echo, R1.Pin_1
  N5: LED1.cathode, R3.Pin_1

notes:
  5V ---> 3V レベル変換
  5V x (1.5 / ( 1 + 1.5 )) = 3V
